# Fritzing sketch gaston_ponteh (saved by Fritzing 0.9.3b)
breadboards: 1

parts:
  M1 = DC Motor  # not connected
  M2 = DC Motor
  S1 = H-Bridge with L298N
  Componente1 = Arduino Uno (Rev3)
  Componente2 = Bluetooth HC-05 Macho
  R1 = Resistor [tolerance=±1% resistance=2.2k power=1.4W package=THT]
  R2 = Resistor [tolerance=±1% resistance=1.5k power=1.4W package=THT]
  Bat1 = battery_holder_dual_18650 [part_number=TBH-18650-2A-P]

nets:
  N1: M2.pin_1, S1.OUT4-Motor2
  GND: S1.GND, Componente1.GND, Componente2.GND, R2.Pin_0, Bat1.+#3
  5V: S1.5V, Componente1.5V, Componente2.VCC
  N2: S1.IN1, Componente1.D7
  N3: S1.IN4, Componente1.D4
  N4: Componente1.D0/RX, Componente2.TXD
  N5: Componente1.D1/TX, R1.Pin_1
  N6: Componente1.VIN, Bat1.+#1
  N7: Componente2.RXD, R1.Pin_0, R2.Pin_1

custom parts:
  H-Bridge with L298N: h-bridge
  battery_holder_dual_18650: TBH-18650-2A-P dual 18650 battery holder.
